# Fritzing sketch CreatorCon-IoT-Device-Fritzing-Details (saved by Fritzing 0.9.3b)
breadboards: 1

parts:
  U3 = NodeMCU V1.0
  R4 = Resistor [tolerance=±5% resistance=390 package=THT]
  R5 = Resistor [tolerance=±5% resistance=390 package=THT]
  R6 = Resistor [tolerance=±5% resistance=390 package=THT]
  LED4 = LED - 5mm [color="Red (633nm)" package="5 mm [THT]"]
  LED5 = LED - 5mm [color="Yellow (595nm)" package="5 mm [THT]"]
  LED6 = LED - 5mm [color="Green (555nm)" package="5 mm [THT]"]
  S2 = Pushbutton [package="[THT]"]
  J3 = Piezo Speaker
  R7 = Rotary Potentiometer (Small) [maximum_resistance=100kΩ package=THT]

nets:
  N1: U3.D1, J3.pin1
  N2: U3.D2, LED4.anode
  N3: U3.D3, LED5.anode
  N4: U3.D4, LED6.anode
  N5: U3.GND, R4.Pin_0, R5.Pin_0, R6.Pin_0, S2.Pin_1, S2.Pin_2, J3.pin2, R7.leg1
  N6: U3.D7, S2.Pin_3, S2.Pin_4
  N7: U3.A0, R7.wiper
  N8: R4.Pin_1, LED5.cathode
  N9: R5.Pin_1, LED6.cathode
  N10: R6.Pin_1, LED4.cathode

custom parts:
  NodeMCU V1.0: ESP8266 based NodeMCU
